# Fritzing sketch HypnoLight (saved by Fritzing 0.9.5d)

parts:
  Power_RGB1 = Prolight RGB 3 Watt Star
  M1 = ESP32-S3-DevKitC-1-N8R8-v1 [part_number=ESP32-S3-DevKitC-1-N8R8-v1]
  Part1 = PicoBuck LED Driver [part_number=COM-11850]
  Part2 = PicoBuck LED Driver [part_number=COM-11850]
  J1 = Screw terminal - 2 pins [package=THT]
  Power_RGB2 = Prolight RGB 3 Watt Star
  Power_RGB3 = Prolight RGB 3 Watt Star
  Power_RGB5 = Prolight RGB 3 Watt Star
  Power_RGB6 = Prolight RGB 3 Watt Star
  Power_RGB4 = Prolight RGB 3 Watt Star
  Part4 = PicoBuck LED Driver [part_number=COM-11850]
  Power_RGB7 = Prolight RGB 3 Watt Star
  Power_RGB8 = Prolight RGB 3 Watt Star
  Power_RGB9 = Prolight RGB 3 Watt Star
  M2 = MT3608 Module
  M3 = MT3608 Module
  T1 = TMP36 Temperature Sensor [package="TO92 [THT]"]
  JP1 = Header 4 [package=screwterminal-3.5mm-4_lock]
  JP2 = Header 4 [package=screwterminal-3.5mm-4_lock]
  JS1 = Generic Jumper Shunt

nets:
  N1: Power_RGB1.R+, Part1.OUT3+
  N2: Power_RGB1.R-, Part1.OUT3-
  N3: M1.pin_1, M1.pin_2, T1.+Vs, JP2.2
  N4: M1.pin_4, Part1.IN1
  N5: M1.pin_5, Part1.IN2
  N6: M1.pin_6, Part1.IN3
  N7: M1.pin_7, Part2.IN1
  N8: M1.pin_8, Part2.IN2
  N9: M1.pin_9, Part2.IN3
  N10: M1.pin_10, Part4.IN1
  N11: M1.pin_11, Part4.IN2
  N12: M1.pin_12, Part4.IN3
  N13: M1.pin_15, T1.Vout
  N14: M1.pin_16, JP1.3
  N15: M1.pin_17, JP1.4
  N16: M1.pin_21, JS1.pin2
  GND: M1.pin_22, M1.pin_44, Part1.GND, Part2.GND, Part4.GND, M2.pin4, T1.GND, JP2.1
  N17: M1.pin_40, JP2.4
  N18: M1.pin_41, JP2.3
  N19: Part1.VIN_+, Part2.VIN_+, J1.pin1, Part4.VIN_+, M2.pin2, M3.pin2
  N20: Part1.VIN_-, Part2.VIN_-, J1.pin2, Part4.VIN_-
  N21: Part1.OUT1+, Power_RGB2.R+
  N22: Part1.OUT1-, Power_RGB2.R-
  N23: Part1.OUT2+, Power_RGB3.R+
  N24: Part1.OUT2-, Power_RGB3.R-
  N25: Part2.OUT1+, Power_RGB5.R+
  N26: Part2.OUT1-, Power_RGB5.R-
  N27: Part2.OUT2+, Power_RGB4.R+
  N28: Part2.OUT2-, Power_RGB4.R-
  N29: Part2.OUT3+, Power_RGB6.R+
  N30: Part2.OUT3-, Power_RGB6.R-
  N31: Part4.OUT1+, Power_RGB8.R+
  N32: Part4.OUT1-, Power_RGB8.R-
  N33: Part4.OUT2+, Power_RGB7.R+
  N34: Part4.OUT2-, Power_RGB7.R-
  N35: Part4.OUT3+, Power_RGB9.R+
  N36: Part4.OUT3-, Power_RGB9.R-
  N37: M2.pin1, M3.pin1
  N38: M2.pin3, JS1.pin1
  N39: M3.pin3, JP1.2
  N40: M3.pin4, JP1.1

custom parts:
  ESP32-S3-DevKitC-1-N8R8-v1: ESP32-S3-DevKitC-1-N8R8-v1 This module is 44pins long (2x22) and 11 pins width.
  PicoBuck LED Driver: The PicoBuck LED Driver is an economical and easy to use driver that will allow you to control and blend three different LEDs on three different channels. Power in supplied to the PicoBuck with a wide range of input voltages (6v to 20v) connected to the VIN header and three inputs for each driver channel (labeled IN1, IN2, and IN3) driven with standard 3.3v or 5v logic. This PicoBuck supports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
  MT3608 Module: MT3608 Boost Converter Module Links: Aerosemi MT3608 2A Step Up Converter datasheet
